# Fritzing sketch Note-Taker Circuit Diagram (saved by Fritzing 0.9.9b)

parts:
  Arduino = Arduino Uno (Rev3)
  Rotary_Encoder = mystery part, 5 pins

nets:
  N1: Arduino.D3_PWM, Rotary_Encoder.pin5
  N2: Arduino.D4, Rotary_Encoder.pin4
  N3: Arduino.D5_PWM, Rotary_Encoder.pin3
  N4: Arduino.D6_PWM, Rotary_Encoder.pin2
  N5: Arduino.D7, Rotary_Encoder.pin1
