# Fritzing sketch Login_Test_Diagram (saved by Fritzing 0.9.9b)
breadboards: 1

parts:
  Arduino = Arduino Uno (Rev3)
  Rotary_Encoder = mystery part, 5 pins [chip_label=Rotary]
  S1 = Pushbutton [package="[SMD]"]
  U1 = mystery part, 8 pins [chip_label=RFID]
  LED1 = smd LED [color="Red (633nm)" package="1206 [SMD]"]
  LED2 = smd LED [color="Green (555nm)" package="1206 [SMD]"]
  R1 = Resistor [tolerance=±5% power=0.25 resistance=100M package=THT]
  R2 = Resistor [tolerance=±5% power=0.25 resistance=100M package=THT]

nets:
  N1: Arduino.D9_PWM, U1.pin2
  N2: Arduino.D10_PWM/SS, U1.pin7
  N3: Arduino.D11_PWM/MOSI, U1.pin5
  N4: Arduino.D12/MISO, U1.pin4
  N5: Arduino.D13/SCK, U1.pin6
  N6: Arduino.D2, Arduino.GND, Rotary_Encoder.pin5, S1.Pin_3, S1.Pin_4, U1.pin3, LED1.cathode, LED2.cathode
  N7: Arduino.D3_PWM, Rotary_Encoder.pin3
  N8: Arduino.D4, R1.Pin_1
  N9: Arduino.D5_PWM, R2.Pin_1
  N10: Arduino.D6_PWM, Rotary_Encoder.pin2
  N11: Arduino.D7, Rotary_Encoder.pin1
  N12: Arduino.3V3, U1.pin1
  N13: Arduino.5V, Rotary_Encoder.pin4
  N14: LED1.anode, R2.Pin_0
  N15: LED2.anode, R1.Pin_0
